# Fritzing sketch solenoid (saved by Fritzing 0.9.3b)
breadboards: 1

parts:
  R1 = Resistor [tolerance=±5% resistance=220 package=THT]  # not connected
  D1 = Rectifier Diode [part_number=1N4001 package="300 mil [THT]"]
  Q1 = PNP-Transistor [package="TO92 [THT]"]  # not connected
  Part1 = Arduino Uno (Rev3)
  L1 = Solenoid
  VCC1 = Battery block 9V
  VCC2 = Battery block 9V

nets:
  N1: D1.cathode, L1.pin2, VCC2.+
  N2: Part1.GND, VCC1.-
